# Fritzing sketch fritzing-sketch (saved by Fritzing 0.9.5d)

parts:
  U1 = ESP 32 DEVKIT DOIT
  U4 = TOUCH [package=touch1]
  U2 = WS2812 RGB LED strip

nets:
  3V3: U1.D4, U1.D15, U1.3V3, U4.T1, U2.VCC, U2.DIN
  GND: U1.GND, U2.GND

custom parts:
  WS2812 RGB LED strip: WS2812 strip
